# Fritzing sketch hology (saved by Fritzing 0.9.3b)
breadboards: 1

parts:
  U1 = ESP32S-HiLetgo [part_number=ESP32S-HiLetgo]
  ESP32_-_Front1 = ESP32 - CAM
  S1 = Momentary Switch [package=ksa_sealed_tac_switch]
  DHT1 = DHT22 Humidity and Temperature Sensor
  Buzzer1 = Buzzer
  OLED_I2C1 = OLED 128x64 I2C Monochrome Display
  Part1 = Soil Moisture Sensor
  VCC1 = Battery

nets:
  VDD: U1.3.3, DHT1.VDD, OLED_I2C1.VDD, Part1.VCC
  N1: U1.GPIO34, Part1.SIG
  N2: U1.GPIO25, Buzzer1.pin1
  N3: U1.GPIO27, S1.4
  GND: U1.GND, ESP32_-_Front1.GND, S1.1, DHT1.GND, Buzzer1.pin2, OLED_I2C1.GND, Part1.GND, VCC1.-
  VIN: U1.VIN, ESP32_-_Front1.5V, VCC1.+
  N4: U1.GPIO4, DHT1.DATA
  N5: U1.GPIO21, OLED_I2C1.SDA
  N6: U1.GPIO22, OLED_I2C1.SCK

custom parts:
  ESP32S-HiLetgo: HiLetgo ESP-WROOM-32 ESP32 ESP-32S Development Board 2.4GHz Dual-Mode WiFi + Bluetooth Dual Cores Microcontroller The ESP32 integrated with Antenna switches, RF Balun, power amplifiers, low-noise amplifiers, filters, and management modules, and the entire solution occupies the least area of PCB. 2.4 GHz Wi-Fi plus Bluetooth dual-mode chip, with TSMC Ultra-low power consumption 40nm technology,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
  ESP32 - CAM: The ESP32-CAM has a very competitive small-size camera module that can operate independently as a minimum system with a footprint of only 27*40.5*4.5mm and a deep sleep current of up to 6mA.
  Battery: Your standard 2x 18650 battery pack (7.4 Volts)
